# Fritzing sketch picotermostato (saved by Fritzing 0.9.6b)
breadboards: 1

parts:
  Mod1 = Raspberry Pi Pico
  Nokia_5110_LCD_Module1 = Nokia 5110 LCD
  R1 = Resistor [tolerance=±5% power=0.25 resistance=100 package=THT]
  S1 = Pushbutton [package="[THT]"]
  S2 = Pushbutton [package="[THT]"]
  S3 = Pushbutton [package="[THT]"]
  Mod2 = KY-019 5V Relay Module [package="Breakout board"]
  DS1 = DS18B20 1-Wire Temperature Sensor [part_number=DS18B20]
  R2 = Resistor [tolerance=±5% power=0.25 resistance=4.7k package=THT]

nets:
  GND: Mod1.pin_3, Mod1.pin_8, Mod1.pin_13, Mod1.pin_18, Mod1.pin_23, Mod1.pin_28, Mod1.pin_33, Mod1.pin_38, Nokia_5110_LCD_Module1.GND, Nokia_5110_LCD_Module1.GND_(out), S1.Pin_1, S1.Pin_2, S2.Pin_1, S2.Pin_2, S3.Pin_1, S3.Pin_2, Mod2.-, DS1.GND
  N1: Mod1.pin_14, DS1.DQ, R2.Pin_0
  N2: Mod1.pin_15, S1.Pin_3, S1.Pin_4
  N3: Mod1.pin_16, S2.Pin_3, S2.Pin_4
  N4: Mod1.pin_17, S3.Pin_3, S3.Pin_4
  N5: Mod1.pin_19, Nokia_5110_LCD_Module1.SCLK
  N6: Mod1.pin_20, Nokia_5110_LCD_Module1.DN(MOSI)
  N7: Mod1.pin_24, Nokia_5110_LCD_Module1.D/C
  N8: Mod1.pin_25, Nokia_5110_LCD_Module1.RST
  N9: Mod1.pin_26, Nokia_5110_LCD_Module1.SCE
  N10: Mod1.pin_27, Mod2.S
  VCC: Mod1.pin_36, Nokia_5110_LCD_Module1.VCC, R1.Pin_1, DS1.VDD, R2.Pin_1
  N11: Mod1.pin_40, Mod2.+
  N12: Nokia_5110_LCD_Module1.LED, Nokia_5110_LCD_Module1.LED_(out), R1.Pin_0

custom parts:
  Raspberry Pi Pico: Raspberry Pi Pico. Based around the RP2040 microcontroller the Pico is a low cost microcontroller device bringing Raspberry Pi quality, cost, and easy of use to the microcontroller space. Jan 2021, Split part in to two versions: tht (this one) and SMD. This one will drill holes for a .1 in header in pcb to allow plugging in the module as well as providing pads to solder the module to the top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
  Nokia 5110 LCD: Nokia 5110 Graphic 84*48 LCD module such as the Sparkfun LCD-10168 or the clones from Ebay. There is example code for the Arduino available from the Sparkfun site in https://learn.sparkfun.com/tutorials/graphic-lcd-hookup-guide This is a 3.3V device, if you are running it from a 5V micro you need a 5V tolorant level translator such as the 74ahc367 to protect the signal imputs. Rafa G. did a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
  KY-019 5V Relay Module: KY-019 5V Relay module, used to control AC circuits. (Special thanks to vanepp for fixing the PCB holes and other errors)
